# Fritzing sketch scheme (saved by Fritzing 0.9.3b)
breadboards: 1

parts:
  BAT1 = 12 battery [package=battery]
  Push = Pushbutton [package="[THT]"]
  Pull = Pushbutton [package="[THT]"]
  U1 = 2-Channel 5v Relay Shield [package=relay-2ch5v10a]
  Linear_actuator = DC Motor
  D1ML1 = WeMos D1 Mini Lite [part_number="WeMos D1 Mini Lite"]
  F1 = FUSE [package=fuse_5mm]
  U2 = DC 5V TO ± 12V Mini DC converter [package=THT]
  F2 = FUSE [package=fuse_5mm]

nets:
  GND: BAT1.-, Push.Pin_3, Push.Pin_4, Pull.Pin_3, Pull.Pin_4, U1.GND, U1.K1-On, U1.K2-On, D1ML1.G, U2.GND
  N1: BAT1.+, F1.2
  N2: Push.Pin_1, Push.Pin_2, D1ML1.D2
  N3: Pull.Pin_1, Pull.Pin_2, D1ML1.D3
  VCC: U1.VCC, U1.IN2, D1ML1.D7, D1ML1.5V, F2.1
  N4: U1.IN1, D1ML1.D5, D1ML1.D6
  N5: U1.K1-In, Linear_actuator.pin_1
  N6: U1.K1-Off, U1.K2-Off, F1.1, U2.Vin
  N7: U1.K2-In, Linear_actuator.pin_2
  N8: U2.-12V, F2.2

notes:
  converter
  12 V DC ➔ 5 V DC
  D1 mini

custom parts:
  12 battery: 12V lead acid type battery, like the Husqvarna YTH2448 12V 35AH battery. This is the mini version 1/4 the size of the actual battery to be closer to typical breadboard parts (around 2in wide rathher than 7in). The pads in pcb are sized to accomidate up to 14ga wire (as these batterys will deliver high currents.)
  2-Channel 5v Relay Shield: 2 Channel 5v Relay Shield w. 2x SPD-06VDC-SD-C
  WeMos D1 Mini Lite: A simple wifi board with 1MB flash based on ESP-8285
  DC 5V TO ± 12V Mini DC converter: DC 5V TO ± 12V Mini DC converter from ebay (search for "DC 5V TO ± 12V Mini DC converter"). Supplies ± 12V at up to 30MA output for op amps or rs232 drivers from a 3 to 5V input (so a battery or 3.3 or 5V power rail) on a micro).
